// Logisim project initial_labs.circ as structural Verilog: 1 circuit, main circuit main
module main (
  input  I_0,
  input  I_1,
  output O_0,
  output O_1,
  output O_2,
  output O_3
);

  and and_1 (O_1, I_0, I_1);
  or or_1 (O_3, I_0, I_1);

  assign O_0 = I_1;
  assign O_2 = I_0;

  // Notes on the sheet:
  //   David Ludwig
  //   CLA 01
  //   x3plus6
endmodule
